# Fritzing sketch project (saved by Fritzing 1.0.4)
breadboards: 1

parts:
  A1 = Wemos S2 Mini [part_number="WeMos D1 Mini Lite"]
  Bauteil1 = GY-VL53L0XV2 Laser Ranger Module
  D1 = LED_BARGRAPH_10 [package=led_bargaph_10]
  R3 = Resistor [tolerance=±5% power=0.25W resistance=220 package=THT]
  R4 = Resistor [tolerance=±5% power=0.25W resistance=220 package=THT]
  R5 = Resistor [tolerance=±5% power=0.25W resistance=220 package=THT]
  R6 = Resistor [tolerance=±5% power=0.25W resistance=220 package=THT]
  R7 = Resistor [tolerance=±5% power=0.25W resistance=220 package=THT]
  R8 = Resistor [tolerance=±5% power=0.25W resistance=220 package=THT]
  R9 = Resistor [tolerance=±5% power=0.25W resistance=220 package=THT]
  R10 = Resistor [tolerance=±5% power=0.25W resistance=220 package=THT]
  R1 = Resistor [tolerance=±5% power=0.25W resistance=220 package=THT]
  R2 = Resistor [tolerance=±5% power=0.25W resistance=220 package=THT]

nets:
  N1: A1.Pin_1, D1.A_C
  N2: A1.Pin_2, D1.B_C
  N3: A1.Pin_3, D1.C_C
  N4: A1.Pin_4, D1.D_C
  N5: A1.Pin_5, D1.E_C
  N6: A1.Pin_6, D1.F_C
  N7: A1.Pin_7, D1.G_C
  N8: A1.Pin_8, Bauteil1.VCC
  N9: A1.Pin_9, D1.H_C
  N10: A1.Pin_10, D1.I_C
  N11: A1.Pin_11, D1.J_C
  N12: A1.Pin_18, A1.Pin_26, Bauteil1.GND
  N13: A1.Pin_21, Bauteil1.SDA
  N14: A1.Pin_22, Bauteil1.SCL
  N15: D1.A_A, R1.Pin_1
  N16: D1.B_A, R2.Pin_1
  N17: D1.C_A, R3.Pin_1
  N18: D1.D_A, R4.Pin_1
  N19: D1.E_A, R5.Pin_1
  N20: D1.F_A, R7.Pin_1
  N21: D1.G_A, R8.Pin_1
  N22: D1.H_A, R6.Pin_1
  N23: D1.I_A, R9.Pin_1
  N24: D1.J_A, R10.Pin_1

custom parts:
  Wemos S2 Mini: A mini wifi board based on the ESP32-S2FN4R2.
  GY-VL53L0XV2 Laser Ranger Module: The GY-VL53L0XV2 is based on the VL53L0X from ST Microelectronics, a time-of-flight ranging system integrated into a compact module.
